# Fritzing sketch Architect_tis (saved by Fritzing 0.9.3b)
breadboards: 1

parts:
  부품1 = Arduino Uno (Rev3)
  Mod1 = KY-015 Temperature & Humidity Sensor Module [package="Breakout board"]
  Disp1 = LBT2088AH [part_number=LBT2088AH]
  U1 = MAX7219 [package=dil24]
  Driver1 = 28BYJ-48 Driver Module [part_number=ULN2003 package=THT]
  SM1 = 28BYJ-48 Stepper Motor [part_number=28BYJ-48]
  R1 = Resistor [tolerance=±5% resistance=10k package=THT]

nets:
  N1: 부품1.D10_PWM/SS, U1.DIG6
  N2: 부품1.D11_PWM/MOSI, U1.DIG4
  N3: 부품1.D13/SCK, U1.GND
  GND: 부품1.GND, Mod1.-, U1.DIG2, Driver1.GND, R1.Pin_0
  N4: 부품1.D2, Driver1.IN4
  N5: 부품1.D3_PWM, Driver1.IN3
  N6: 부품1.D4, Driver1.IN2
  N7: 부품1.D5_PWM, Driver1.IN1
  N8: 부품1.D6_PWM, Mod1.S
  5V: 부품1.5V, Mod1.Vin, U1.DIN, Driver1.Vmotor
  N9: Disp1.pin1, U1.DOUT
  N10: Disp1.pin2, U1.SEGD
  N11: Disp1.pin_3, U1.SEGDP
  N12: Disp1.pin_4, U1.SEGE
  N13: Disp1.pin_5, U1.SEGC
  N14: Disp1.pin_6, U1.VCC
  N15: Disp1.pin_7, U1.ISET
  N16: Disp1.pin_8, U1.SEGG
  N17: U1.DIG0, R1.Pin_1
  N18: Driver1.blue-pin, SM1.blue-pin
  N19: Driver1.pink-pin, SM1.pink-pin
  N20: Driver1.yellow-pin, SM1.yellow-pin
  N21: Driver1.orange-pin, SM1.orange-pin
  N22: Driver1.red-pin, SM1.red-pin

custom parts:
  KY-015 Temperature & Humidity Sensor Module: KY-015 temperature and humidity sensor module, provides a low-latency serial interface to measure humidity and temperature.
  28BYJ-48 Driver Module: ULN2003 Driver Module for the 28BYJ-48 Unipolar Stepper Motor LED A - Blue wire - Bottom coil left LED B - Pink wire - Top coil left LED C - Yellow wire - Bottom coil right LED D - Orange wire - Top coil right Common rail - red Connector pins: blue - pink - yellow - orange - red Control pins - IN1 to IN4 Power pins - GND & Vmotor (5-12V) On/Off jumper (if removed, power to motor is cut).
  28BYJ-48 Stepper Motor: Unipolar Stepper Motor 28BYJ-48 Top coil - pink & orange Bottom coil - blue & yellow Common rail - red Connector pins: blue - pink - yellow - orange - red
